# Fritzing sketch Sketch (saved by Fritzing 1.0.6)
breadboards: 1

parts:
  R1 = Resistor [tolerance=±5% resistance=4.7k power=0.25W package=THT]
  R2 = Resistor [tolerance=±5% resistance=1k power=0.25W package=THT]
  A1 = ESP32 DevKitc V4
  12V_GND_Ta_PWM = Camdenboss CTB0158-4 [part_number="+12V GND Tacho PWM" package=THT]
  M1 = RioRand LM2596
  Q1 = npn-Powertransistor [part_number=2N2222A package="TO220 [THT]"]
  J2 = Camdenboss CTB0158-4 [part_number=CTB0158-4 package=THT]
  DS2 = DS18B20 1-Wire Temperature Sensor [part_number=DS18B20]
  HLK-PM4 = HLK-PM12 [part_number=HLK-PM12]

nets:
  N1: R1.Pin_0, A1.Pin_29, J2.pin3
  N2: R1.Pin_1, A1.Pin_1, J2.pin1
  N3: R2.Pin_0, A1.Pin_26
  N4: R2.Pin_1, Q1.base
  N5: A1.Pin_14, A1.Pin_32, A1.Pin_38, M1.Pin_4, Q1.collector, J2.pin2
  N6: A1.Pin_19, M1.Pin_3
  N7: A1.Pin_33, 12V_GND_Ta_PWM.pin2
  N8: 12V_GND_Ta_PWM.pin1, Q1.emitter
  N9: 12V_GND_Ta_PWM.pin3, M1.Pin_2, HLK-PM4.-Vo
  N10: 12V_GND_Ta_PWM.pin4, M1.Pin_1, HLK-PM4.+Vo
  N11: J2.terminal_1, DS2.VDD
  N12: J2.terminal_2, DS2.GND
  N13: J2.terminal_3, DS2.DQ

custom parts:
  ESP32 DevKitc V4: ESP32-DevKitC board with ESP32-WROOM-32 module. ESP32-DevKitC V4 is a small-sized ESP32-based development board produced by Espressif. Most of the pins on the ESP module are broken out to the pin headers on the board. The pins D0, D1, D2, D3, CMD and CLK are used internally for communication between ESP32 and SPI flash memory. They are grouped on both sides near the USB connector. Avoid using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
  HLK-PM12: AC-DC 220V to 12V Step-Down Power Supply Module forked from Iyad Nahas
