# Fritzing sketch Schematic (saved by Fritzing 0.9.5d)
circuit board: 8.46667cm x 5.64444cm
breadboards: 1

parts:
  R1 = Resistor [tolerance=±5% resistance=10k package=THT]
  R2 = Resistor [tolerance=±5% resistance=100 package=THT]
  D1 = LTE-302 [part_number=IR-LED package=lte-302]
  Q1 = LTR-301 [part_number="Short + / Long GND" package=ltr-301]
  R3 = Resistor [tolerance=±5% resistance=220 package=THT]
  U1 = XIAO ESP32C6 [part_number=" XIAO ESP32C6"]
  R4 = Resistor [tolerance=±5% resistance=68 package=THT]
  R5 = Resistor [tolerance=±5% resistance=68 package=THT]
  LED1 = RGB LED (com. cathode, rgb) [package="5 mm [THT]"]

nets:
  N1: R1.Pin_0, D1.A, U1.3V3
  N2: R1.Pin_1, Q1.C, U1.D5
  N3: R2.Pin_0, U1.D8
  N4: R2.Pin_1, D1.C
  N5: Q1.E, U1.GND, LED1.common_cathode
  N6: R3.Pin_0, U1.D7
  N7: R3.Pin_1, LED1.red_anode
  N8: U1.D9, R4.Pin_0
  N9: U1.D10, R5.Pin_0
  N10: R4.Pin_1, LED1.green_anode
  N11: R5.Pin_1, LED1.blue_anode

custom parts:
  XIAO ESP32C6: XIAO ESP32C6 is a cost-effective MCU based on Espressif’s ESP32-C6. This compact MCU excels in Matter-compliant smart home applications with its support for various wireless connectivity (2.4GHz Wi-Fi 6, BLE 5.0, Zigbee, and Thread). Designed with the thumb-size footprint and a single-sided mount of the XIAO Series, it's perfect for space-limited projects. Encrypted on the chip, the XIAO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
