# Fritzing sketch DS18B20 (saved by Fritzing 1.0.6)
breadboards: 1

parts:
  U1 = XIAO ESP32C6 [part_number=" XIAO ESP32C6"]
  X1 = USB Connectors [package=usb-a-pcb]
  DS2 = DS18B20 1-Wire Temperature Sensor [part_number=DS18B20]
  U2 = WS2812 RGB LED strip

nets:
  N1: U1.D7, U2.DIN
  N2: U1.D10, DS2.DQ
  3V3: U1.3V3, DS2.VDD
  GND: U1.GND, X1.GND, DS2.GND, U2.GND
  5V: U1.5V, X1.D+, U2.VCC

custom parts:
  XIAO ESP32C6: XIAO ESP32C6 is a cost-effective MCU based on Espressif’s ESP32-C6. This compact MCU excels in Matter-compliant smart home applications with its support for various wireless connectivity (2.4GHz Wi-Fi 6, BLE 5.0, Zigbee, and Thread). Designed with the thumb-size footprint and a single-sided mount of the XIAO Series, it's perfect for space-limited projects. Encrypted on the chip, the XIAO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
  WS2812 RGB LED strip: WS2812 strip
